// Logisim project alu.circ as structural Verilog: 1 circuit, main circuit main
module main (
  input  [2:0] S,
  input  [7:0] A,
  input  [7:0] B,
  output ZF,
  output VF,
  output [7:0] out_6
);

  wire and_1_out, not_1_out, or_2_out;
  wire [7:0] adder_1_out, and_2_out, bit_extender_1_out, multiplexer_1_out, multiplexer_2_out, not_2_out,
       or_1_out;

  assign bit_extender_1_out = {{7{1'b0}}, S[1]};  // Bit_Extender bit_extender_1
  not not_1 (not_1_out, S[1]);
  and and_1 (and_1_out, S[0], not_1_out, S[2]);
  Multiplexer #(.select(3), .width(8)) multiplexer_1 (
    .in0(A), .in1(B), .in2(A), .in3(B), .in4(A), .in5(A), .out(multiplexer_1_out), .sel(S));  // open: in6, in7, en
  Multiplexer #(.select(3), .width(8)) multiplexer_2 (
    .in0(bit_extender_1_out), .in1(bit_extender_1_out), .in2(bit_extender_1_out), .in3(bit_extender_1_out),
    .in4(B), .in5(not_2_out), .out(multiplexer_2_out), .sel(S));  // open: in6, in7, en
  assign not_2_out = ~B;  // NOT_Gate not_2, 8 bits wide
  assign and_2_out = B & A;  // AND_Gate and_2, 8 bits wide
  assign or_1_out = B | A;  // OR_Gate or_1, 8 bits wide
  Adder adder_1 (.a(multiplexer_1_out), .b(multiplexer_2_out), .out(adder_1_out), .cin(and_1_out), .cout(VF));
  Multiplexer #(.select(3), .width(8)) multiplexer_3 (
    .in0(adder_1_out), .in1(adder_1_out), .in2(adder_1_out), .in3(adder_1_out), .in4(adder_1_out),
    .in5(adder_1_out), .in6(and_2_out), .in7(or_1_out), .out(out_6), .sel(S));  // open: en
  or or_2 (or_2_out, out_6[0], out_6[1], out_6[2], out_6[3], out_6[4], out_6[5], out_6[6], out_6[7]);
  not not_3 (ZF, or_2_out);

  // Notes on the sheet:
  //   Homework #2
  //   Calvin Spencer & Chase Coley
  //   Out
endmodule
