// Logisim project month.circ as structural Verilog: 1 circuit, main circuit main
module main (
  input  M0,
  input  M1,
  input  M2,
  input  M3,
  output Y
);

  wire and_1_out, and_2_out, and_3_out, and_4_out, and_5_out, and_6_out, and_7_out, not_1_out, not_2_out,
       not_3_out, not_4_out, not_5_out, not_6_out, not_7_out, not_8_out, not_9_out, not_10_out, not_11_out,
       not_12_out, not_13_out, not_14_out, not_15_out, or_1_out, or_2_out;

  not not_1 (not_1_out, M1);
  and and_1 (and_1_out, M0, not_1_out, not_2_out, not_3_out);
  not not_2 (not_2_out, M2);
  not not_3 (not_3_out, M3);
  and and_2 (and_2_out, M0, M1, not_4_out, not_5_out);
  not not_4 (not_4_out, M2);
  not not_5 (not_5_out, M3);
  and and_3 (and_3_out, M0, not_6_out, M2, not_7_out);
  not not_6 (not_6_out, M1);
  not not_7 (not_7_out, M3);
  and and_4 (and_4_out, M0, M1, M2, M2, not_8_out);
  not not_8 (not_8_out, M3);
  not not_9 (not_9_out, M0);
  not not_10 (not_10_out, M1);
  not not_11 (not_11_out, M2);
  and and_5 (and_5_out, not_9_out, not_10_out, not_11_out, M3);
  not not_12 (not_12_out, M0);
  and and_6 (and_6_out, not_12_out, M1, not_13_out, M3);
  not not_13 (not_13_out, M2);
  not not_14 (not_14_out, M0);
  not not_15 (not_15_out, M1);
  and and_7 (and_7_out, not_14_out, not_15_out, M2, M3);
  or or_1 (or_1_out, and_1_out, and_2_out, and_3_out);
  or or_2 (or_2_out, and_4_out, and_5_out, and_6_out, and_7_out);
  or or_3 (Y, or_1_out, or_1_out, or_2_out);

  // Notes on the sheet:
  //   M0M3'M2'M1'
  //   M1M0M3'M2'
  //   M2M0M3'M1'
  //   M2M1M0M3'
  //   M3M2'M1'M0'
  //   M3M1M2'M0'
  //   M3M2M1'M0'
endmodule
