// Logisim project xor.circ as structural Verilog: 1 circuit, main circuit main
module main (
  input  X,
  input  Y,
  output Z
);

  wire nand_1_out, nand_2_out, X_prime_out, Y_prime_out;

  nand X_prime (X_prime_out, X, X);
  nand Y_prime (Y_prime_out, Y, Y);
  nand nand_1 (nand_1_out, X_prime_out, Y);
  nand nand_2 (nand_2_out, X, Y_prime_out);
  nand nand_3 (Z, nand_1_out, nand_2_out);

  // Notes on the sheet:
  //   Calvin Spencer: XOR from NAND Gates
endmodule
