// Logisim project ALU.circ as structural Verilog: 3 circuits, main circuit CPU
module ALU (
  input  [7:0] A,
  input  [7:0] B,
  input  [2:0] S,
  output [7:0] Out,
  output ZF,
  output VF
);

  wire A7, A_B, A_B_t, and_6_out, and_7_out, B7, Inc_A, Inc_B, not_5_out, not_6_out, not_7_out, Not_S0,
       Not_S1, Not_S2, or_2_out, or_3_out, R7;
  wire [6:0] adder_1_out, multiplexer_1_out, multiplexer_2_out;
  wire [7:0] and_3_out, multiplexer_3_out, not_1_out, or_1_out;

  assign not_1_out = ~B;  // NOT_Gate not_1, 8 bits wide
  and and_1 (Inc_A, Not_S2, S[1], Not_S0);
  and and_2 (Inc_B, Not_S2, S[1], S[0]);
  Multiplexer #(.width(8), .enable("false")) multiplexer_1 (
    .in0(A), .in1(8'h1), .out({A7, multiplexer_1_out}), .sel(Inc_B));
  Multiplexer #(.width(8), .enable("false")) multiplexer_2 (
    .in0(multiplexer_3_out), .in1(not_1_out), .out({B7, multiplexer_2_out}), .sel(A_B_t));
  Multiplexer #(.width(8), .enable("false")) multiplexer_3 (.in0(B), .in1(8'h1), .out(multiplexer_3_out), .sel(Inc_A));
  assign and_3_out = A & B;  // AND_Gate and_3, 8 bits wide
  assign or_1_out = A | B;  // OR_Gate or_1, 8 bits wide
  Adder adder_1 (
    .a({A7, multiplexer_1_out}), .b({B7, multiplexer_2_out}), .out({R7, adder_1_out}), .cin(A_B_t));  // open: cout
  not not_2 (Not_S0, S[0]);
  not not_3 (Not_S1, S[1]);
  not not_4 (Not_S2, S[2]);
  and and_4 (A_B, S[2], Not_S1, Not_S0);
  and and_5 (A_B_t, S[2], Not_S1, S[0]);
  Multiplexer #(.select(3), .width(8), .enable("false")) multiplexer_4 (
    .in0(A), .in1(B), .in2({R7, adder_1_out}), .in3({R7, adder_1_out}), .in4({R7, adder_1_out}),
    .in5({R7, adder_1_out}), .in6(and_3_out), .in7(or_1_out), .out(Out), .sel(S));
  not not_5 (not_5_out, A7);
  not not_6 (not_6_out, B7);
  not not_7 (not_7_out, R7);
  and and_6 (and_6_out, not_5_out, R7, not_6_out);
  and and_7 (and_7_out, A7, not_7_out, B7);
  nor nor_1 (ZF, Out[0], Out[1], Out[2], Out[3], Out[4], Out[5], Out[6], Out[7]);
  or or_2 (or_2_out, and_6_out, and_7_out);
  or or_3 (or_3_out, Inc_A, Inc_B, A_B, A_B_t);
  and and_8 (VF, or_2_out, or_3_out);

  // Notes on the sheet:
  //   Opcode Detectors - used to detect which arithmetic op we are performing
  //   Extract MSB of operands
  //   and result for overflow
  //   detection.
  //   8-bit ALU with zero and overflow detection
  //   Author: RR
  //   Logic for VF: We performed addition,
  //   increment, or subtraction and there was a sign
  //   mismatch between operands and result
endmodule

module control (
  input  [4:0] MBR,
  input  RST,
  input  CLK,
  output [2:0] ALU_Select,
  output [1:0] B_Select,
  output A,
  output B,
  output MBR_2,
  output PC,
  output Out,
  output [4:0] next,
  output Halt
);

  wire not_1_out;
  wire [4:0] multiplexer_1_out, register_2_q_2;
  wire [10:10] register_2_q;
  wire [15:0] rom_1_data;

  Multiplexer #(.width(5)) multiplexer_1 (
    .in0(register_2_q_2), .in1(MBR), .out(multiplexer_1_out), .sel(register_2_q[10]));  // open: en
  Register #(.width(5)) register_1 (.D(multiplexer_1_out), .Q(next), .clk(CLK), .clr(RST));  // open: en
  not not_1 (not_1_out, next[1]);
  ROM #(.addrWidth(5), .dataWidth(16)) rom_1 (.addr(next), .data(rom_1_data));  // open: sel
  and and_1 (Halt, next[0], not_1_out, next[2], next[3], next[4]);
  Register #(.width(16), .trigger("falling")) register_2 (
    .D(rom_1_data), .Q({register_2_q_2, register_2_q[10], ALU_Select, B_Select, A, B, MBR_2, PC, Out}),
    .clk(CLK), .clr(RST));  // open: en

  // Notes on the sheet:
  //   Next State
  //   DSP
  //   SPC
  //   ROM
  //   11101
  //   contents of rom_1 (hex, n*v repeats v):
  //   804 11c0 19c2 400 28e0 30f0 0 4000 4801 0 5804 60a0 68a2 0 7804 81c0 89c2 90a0 98b0 0 a900 b110 0
  //   c000 c808 0 da00 e210 0 e800
  //   IR
endmodule

module CPU (
  input  [7:0] Input,
  input  in_2,
  input  [7:0] Out,
  output halt
);

  wire A_Enable, B_Enable, CLK, MBR_Enable, Out_Enable, PC_Enable;
  wire [1:0] B_Select;
  wire [2:0] ALU_Select;
  wire [4:0] MBR;
  wire [7:0] alu_1_out, Data, multiplexer_1_out, register_1_q, register_2_q, register_4_q;
  wire [7:5] register_3_q;

  Register register_1 (.D(alu_1_out), .en(A_Enable), .Q(register_1_q), .clk(CLK), .clr(in_2));
  Register register_2 (.D(alu_1_out), .en(B_Enable), .Q(register_2_q), .clk(CLK), .clr(in_2));
  Register register_3 (.D(Data), .en(MBR_Enable), .Q({register_3_q, MBR}), .clk(CLK), .clr(in_2));
  Register register_4 (.D(alu_1_out), .en(PC_Enable), .Q(register_4_q), .clk(CLK), .clr(in_2));
  Register register_5 (.D(alu_1_out), .en(Out_Enable), .Q(Out), .clk(CLK), .clr(in_2));
  // Probe on B_Select
  // Probe on register_1_q
  Multiplexer #(.select(2), .width(8)) multiplexer_1 (
    .in0(register_2_q), .in1({register_3_q, MBR}), .in2(register_4_q), .in3(Input), .out(multiplexer_1_out),
    .sel(B_Select));  // open: en
  // Probe on multiplexer_1_out
  Hex_Digit_Display hex_digit_display_1 (.value(Out[7:4]));  // open: dp
  Hex_Digit_Display hex_digit_display_2 (.value(Out[3:0]));  // open: dp
  ALU alu_1 (.A(register_1_q), .B(multiplexer_1_out), .Out(alu_1_out), .S(ALU_Select));  // open: ZF, VF
  // Probe on ALU_Select
  control control_1 (
    .MBR(MBR), .RST(in_2), .CLK(CLK), .Halt(halt), .Out(Out_Enable), .PC(PC_Enable), .MBR_2(MBR_Enable),
    .B(B_Enable), .A(A_Enable), .B_Select(B_Select), .ALU_Select(ALU_Select));  // open: next
  Clock clock_1 (.out(CLK));
  RAM ram_1 (.addr(register_4_q), .data(Data));  // open: sel, clk, ld, clr

  // Other names for the same wires on the sheet: RST = in_2

  // Notes on the sheet:
  //   CPU
  //   Calvin Spencer & Chase Coley
  //   A
  //   B
  //   MBR
  //   PC
  //   OUT
  //   Program Store
endmodule
