// Logisim project majority.circ as structural Verilog: 1 circuit, main circuit main
module main (
  input  X,
  input  Y,
  input  Z,
  output Majority
);

  wire XY_out, XZ_out, YZ_out;

  and YZ (YZ_out, Y, Z);
  and XZ (XZ_out, X, Z);
  and XY (XY_out, Y, X);
  or or_1 (Majority, XY_out, XZ_out, YZ_out);
endmodule
